# Fritzing sketch PIA_New (saved by Fritzing 0.9.3b)
breadboards: 1

parts:
  Part2 = Arduino Mega ADK (Rev3)
  Rojo3 = LED - 5mm [color="Red (633nm)" package="5 mm [THT]"]
  Rojo4 = LED - 5mm [color="Red (633nm)" package="5 mm [THT]"]
  Amar3 = LED - 5mm [color="Yellow (595nm)" package="5 mm [THT]"]
  Amar4 = LED - 5mm [color="Yellow (595nm)" package="5 mm [THT]"]
  Verde3 = LED - 5mm [color="Green (570nm)" package="5 mm [THT]"]
  Verde4 = LED - 5mm [color="Green (570nm)" package="5 mm [THT]"]
  R8 = Resistor [tolerance=±5% resistance=220 package="2010 [SMD]"]
  R9 = Resistor [tolerance=±5% resistance=220 package="2010 [SMD]"]
  R10 = Resistor [tolerance=±5% resistance=220 package="2010 [SMD]"]
  R11 = Resistor [tolerance=±5% resistance=220 package="2010 [SMD]"]
  R12 = Resistor [tolerance=±5% resistance=220 package="2010 [SMD]"]
  R13 = Resistor [tolerance=±5% resistance=220 package="2010 [SMD]"]

nets:
  N1: Part2.D10_PWM, Rojo3.anode
  N2: Part2.D9_PWM, Amar3.anode
  N3: Part2.D8_PWM, Verde3.anode
  N4: Part2.GND, R8.Pin_1, R9.Pin_1, R10.Pin_1, R11.Pin_1, R12.Pin_1, R13.Pin_1
  N5: Part2.D5_PWM, Verde4.anode
  N6: Part2.D6_PWM, Amar4.anode
  N7: Part2.D7_PWM, Rojo4.anode
  N8: Rojo3.cathode, R12.Pin_0
  N9: Rojo4.cathode, R9.Pin_0
  N10: Amar3.cathode, R13.Pin_0
  N11: Amar4.cathode, R10.Pin_0
  N12: Verde3.cathode, R8.Pin_0
  N13: Verde4.cathode, R11.Pin_0

// code stored in the sketch: Pia_New.ino
// Pines de arduino
int green1 = 5;
int yellow1 = 6;
int red1 = 7;
int green2 = 8;
int yellow2 = 9;
int red2 = 10;
void turnoff(int led){
  // Apaga LED
  digitalWrite(led, LOW);
}
void turnon(int led){
  // Prende LED
  digitalWrite(led, HIGH);
}
void switchled(int ledoff,int ledon,int wait){
  // Apaga un led, prende otro y espera <wait> milisegundos
  turnoff(ledoff);
  turnon(ledon);
  delay(wait);
}
void green2red(int green,int yellow,int red){
  // Secuencia de verde a amarillo a rojo
  switchled(red,green,5000);
  switchled(green,yellow,1500);
  switchled(yellow,red,500);
}
 void empezar(){
  // Define estado inicial e inicia secuencia de transformaci?n de LEDs
  turnon(green1);
  turnon(red2);
  green2red(green1,yellow1,red1);
  green2red(green2,yellow2,red2);
}

void setup(){
  pinMode(green1, OUTPUT);
  pinMode(yellow1, OUTPUT);
  pinMode(red1, OUTPUT);
  pinMode(green2, OUTPUT);
  pinMode(yellow2, OUTPUT);
  pinMode(red2, OUTPUT);
}

void loop(){
  // Inicia programa en loop indefinidamente
  empezar();
}
